// Logisim project stack_logical_normal.circ as structural Verilog: 15 circuits, main circuit main
module main (
  input  CLK,
  input  RESET,
  input  [1:0] COMMAND,
  input  [2:0] INDEX,
  input  [3:0] IO_DATA_in,
  output [3:0] IO_DATA_out
);

  stack stack_1 (
    .CLK(CLK), .RESET(RESET), .COMMAND(COMMAND), .INDEX(INDEX), .IO_DATA_in(IO_DATA_in),
    .IO_DATA_out(IO_DATA_out));
endmodule

module stack (
  input  CLK,
  input  RESET,
  input  [1:0] COMMAND,
  input  [2:0] INDEX,
  input  [3:0] IO_DATA_in,
  output [3:0] IO_DATA_out
);

  wire and_1_out, and_2_out, demux_1_i, demux_1_ii, demux_1_iii, demux_1_iv, demux_1_o, gate_1_open_gate_n,
       transmission_1_p4, xor_1_out;
  wire [2:0] get_val_1_out_index, head_1_out_head, ind_down_1_ind_out;
  wire [3:0] four_bit_cell_1_outval, four_bit_cell_2_outval, four_bit_cell_3_outval, four_bit_cell_4_outval,
       four_bit_cell_5_outval, mux_1_out_val;

  xor xor_1 (xor_1_out, COMMAND[0], COMMAND[1]);
  and and_1 (and_1_out, COMMAND[0], xor_1_out);
  Head head_1 (.up_down(and_1_out), .T(xor_1_out), .clk(CLK), .Reset(RESET), .Out_head(head_1_out_head));
  and and_2 (and_2_out, COMMAND[0], COMMAND[1]);
  Demux demux_1 (
    .Val(and_1_out), .Index(head_1_out_head), .O(demux_1_o), .I(demux_1_i), .II(demux_1_ii),
    .III(demux_1_iii), .IV(demux_1_iv));
  Four_bit_cell four_bit_cell_1 (
    .W_R(demux_1_o), .clk(CLK), .Reset(RESET), .D(IO_DATA_in), .OutVal(four_bit_cell_1_outval));
  Four_bit_cell four_bit_cell_2 (
    .W_R(demux_1_i), .clk(CLK), .Reset(RESET), .D(IO_DATA_in), .OutVal(four_bit_cell_2_outval));
  Four_bit_cell four_bit_cell_3 (
    .W_R(demux_1_ii), .clk(CLK), .Reset(RESET), .D(IO_DATA_in), .OutVal(four_bit_cell_3_outval));
  Four_bit_cell four_bit_cell_4 (
    .W_R(demux_1_iii), .clk(CLK), .Reset(RESET), .D(IO_DATA_in), .OutVal(four_bit_cell_4_outval));
  Four_bit_cell four_bit_cell_5 (
    .W_R(demux_1_iv), .clk(CLK), .Reset(RESET), .D(IO_DATA_in), .OutVal(four_bit_cell_5_outval));
  ind_down ind_down_1 (.ind(INDEX), .down_flag(and_2_out), .ind_out(ind_down_1_ind_out));
  get_val get_val_1 (.Head(head_1_out_head), .Index(ind_down_1_ind_out), .out_index(get_val_1_out_index));
  gate gate_1 (.comO(COMMAND[0]), .comI(COMMAND[1]), .clk(CLK), .open_gate_n(gate_1_open_gate_n));
  Mux mux_1 (
    .O(four_bit_cell_1_outval), .I(four_bit_cell_2_outval), .II(four_bit_cell_3_outval),
    .III(four_bit_cell_4_outval), .IV(four_bit_cell_5_outval), .Index(get_val_1_out_index),
    .Out_val(mux_1_out_val));
  // Transmission_Gate #(.width(4)) transmission_1: pin names not known; wires that end beside it: gate_1_open_gate_n, mux_1_out_val, IO_DATA_in, transmission_1_p4
  not not_1 (transmission_1_p4, gate_1_open_gate_n);

  assign IO_DATA_out = IO_DATA_in;

  // Notes on the sheet:
  //   your circuit must be here
endmodule

module RS_trigger (
  input  Set,
  input  R,
  input  c,
  input  S,
  input  Reset,
  output Q,
  output nQ
);

  wire and_1_out, and_2_out, and_3_out, and_4_out, or_1_out, or_2_out;

  and and_1 (and_1_out, R, c);
  and and_2 (and_2_out, c, S);
  and and_3 (and_3_out, ~Set, and_1_out);  // AND_Gate
  or or_1 (or_1_out, Set, and_2_out);
  or or_2 (or_2_out, and_3_out, Reset);
  and and_4 (and_4_out, or_1_out, ~Reset);  // AND_Gate
  nor nor_1 (Q, or_2_out, nQ);
  nor nor_2 (nQ, Q, and_4_out);
endmodule

module D_trigger (
  input  D,
  input  clk,
  input  Reset,
  output Q
);

  wire and_1_out, and_2_out, and_3_out, nor_2_out, or_1_out;

  and and_1 (and_1_out, ~D, clk);  // AND_Gate
  and and_2 (and_2_out, clk, D);
  or or_1 (or_1_out, and_1_out, Reset);
  and and_3 (and_3_out, and_2_out, ~Reset);  // AND_Gate
  nor nor_1 (Q, or_1_out, nor_2_out);
  nor nor_2 (nor_2_out, Q, and_3_out);
endmodule

module T_trigger (
  input  Set,
  input  T,
  input  clk,
  input  Reset,
  output Q,
  output nQ
);

  wire and_1_out, and_2_out, not_1_out, rs_trigger_1_nq, rs_trigger_1_q;

  and and_1 (and_1_out, nQ, T);
  and and_2 (and_2_out, T, Q);
  not not_1 (not_1_out, clk);
  RS_trigger rs_trigger_1 (
    .Set(Set), .R(and_2_out), .c(clk), .S(and_1_out), .Reset(Reset), .Q(rs_trigger_1_q), .nQ(rs_trigger_1_nq));
  RS_trigger rs_trigger_2 (
    .Set(Set), .R(rs_trigger_1_nq), .c(not_1_out), .S(rs_trigger_1_q), .Reset(Reset), .Q(Q), .nQ(nQ));

  // Notes on the sheet:
  //   T: pull=down
  //   Reset: pull=down
  //   Q: pull=down
  //   nQ: pull=down
endmodule

module Four_bit_cell (
  input  W_R,
  input  clk,
  input  Reset,
  input  [3:0] D,
  output [3:0] OutVal
);

  wire and_1_out;

  and and_1 (and_1_out, W_R, clk);
  D_trigger d_trigger_1 (.D(D[0]), .clk(and_1_out), .Reset(Reset), .Q(OutVal[0]));
  D_trigger d_trigger_2 (.D(D[1]), .clk(and_1_out), .Reset(Reset), .Q(OutVal[1]));
  D_trigger d_trigger_3 (.D(D[2]), .clk(and_1_out), .Reset(Reset), .Q(OutVal[2]));
  D_trigger d_trigger_4 (.D(D[3]), .clk(and_1_out), .Reset(Reset), .Q(OutVal[3]));
endmodule

module Demux (
  input  Val,
  input  [2:0] Index,
  output O,
  output I,
  output II,
  output III,
  output IV
);

  wire and_1_out, and_2_out, and_3_out, and_4_out, and_5_out, and_6_out, and_7_out, and_8_out, and_9_out,
       and_10_out;

  and and_1 (and_1_out, ~Index[2], ~Index[1]);  // AND_Gate
  and and_2 (and_2_out, and_1_out, ~Index[0]);  // AND_Gate
  and and_3 (and_3_out, ~Index[2], ~Index[1]);  // AND_Gate
  and and_4 (and_4_out, and_3_out, Index[0]);
  and and_5 (and_5_out, ~Index[2], Index[1]);  // AND_Gate
  and and_6 (and_6_out, and_5_out, ~Index[0]);  // AND_Gate
  and and_7 (and_7_out, ~Index[2], Index[1]);  // AND_Gate
  and and_8 (and_8_out, and_7_out, Index[0]);
  and and_9 (and_9_out, Index[2], ~Index[1]);  // AND_Gate
  and and_10 (and_10_out, and_9_out, ~Index[0]);  // AND_Gate
  and and_11 (O, and_2_out, Val);
  and and_12 (I, and_4_out, Val);
  and and_13 (II, and_6_out, Val);
  and and_14 (III, and_8_out, Val);
  and and_15 (IV, and_10_out, Val);
endmodule

module Mux (
  input  [3:0] O,
  input  [3:0] I,
  input  [3:0] II,
  input  [3:0] III,
  input  [3:0] IV,
  input  [2:0] Index,
  output [3:0] Out_val
);

  wire and_1_out, and_2_out, and_3_out, and_4_out, and_5_out, and_6_out, and_7_out, and_8_out, and_9_out,
       and_10_out;
  wire [3:0] bit_and_1_out_val, bit_and_2_out_val, bit_and_3_out_val, bit_and_4_out_val, bit_and_5_out_val,
       or_1_out, or_2_out, or_3_out;

  and and_1 (and_1_out, ~Index[2], ~Index[1]);  // AND_Gate
  and and_2 (and_2_out, and_1_out, ~Index[0]);  // AND_Gate
  and and_3 (and_3_out, ~Index[2], ~Index[1]);  // AND_Gate
  and and_4 (and_4_out, and_3_out, Index[0]);
  and and_5 (and_5_out, ~Index[2], Index[1]);  // AND_Gate
  and and_6 (and_6_out, and_5_out, ~Index[0]);  // AND_Gate
  and and_7 (and_7_out, ~Index[2], Index[1]);  // AND_Gate
  and and_8 (and_8_out, and_7_out, Index[0]);
  and and_9 (and_9_out, Index[2], ~Index[1]);  // AND_Gate
  and and_10 (and_10_out, and_9_out, ~Index[0]);  // AND_Gate
  bit_and bit_and_1 (.Val(O), .\bit (and_2_out), .Out_val(bit_and_1_out_val));
  bit_and bit_and_2 (.Val(I), .\bit (and_4_out), .Out_val(bit_and_2_out_val));
  bit_and bit_and_3 (.Val(II), .\bit (and_6_out), .Out_val(bit_and_3_out_val));
  bit_and bit_and_4 (.Val(III), .\bit (and_8_out), .Out_val(bit_and_4_out_val));
  bit_and bit_and_5 (.Val(IV), .\bit (and_10_out), .Out_val(bit_and_5_out_val));
  assign or_1_out = bit_and_1_out_val | bit_and_2_out_val;  // OR_Gate or_1, 4 bits wide
  assign or_2_out = bit_and_3_out_val | bit_and_4_out_val;  // OR_Gate or_2, 4 bits wide
  assign or_3_out = or_1_out | or_2_out;  // OR_Gate or_3, 4 bits wide
  assign Out_val = or_3_out | bit_and_5_out_val;  // OR_Gate or_4, 4 bits wide
endmodule

module bit_and (
  input  [3:0] Val,
  input  \bit ,
  output [3:0] Out_val
);

  and and_1 (Out_val[0], Val[0], \bit );
  and and_2 (Out_val[1], Val[1], \bit );
  and and_3 (Out_val[2], Val[2], \bit );
  and and_4 (Out_val[3], Val[3], \bit );
endmodule

module half_sub (
  input  A,
  input  B,
  output \bit ,
  output borrow
);

  xor xor_1 (\bit , A, B);
  and and_1 (borrow, ~A, B);  // AND_Gate
endmodule

module full_sub (
  input  A,
  input  B,
  input  Bin,
  output \bit ,
  output Bout
);

  wire half_sub_1_bit, half_sub_1_borrow, half_sub_2_borrow;

  half_sub half_sub_1 (.A(A), .B(B), .\bit (half_sub_1_bit), .borrow(half_sub_1_borrow));
  half_sub half_sub_2 (.A(half_sub_1_bit), .B(Bin), .\bit (\bit ), .borrow(half_sub_2_borrow));
  or or_1 (Bout, half_sub_2_borrow, half_sub_1_borrow);
endmodule

module get_val (
  input  [2:0] Head,
  input  [2:0] Index,
  output [2:0] out_index
);

  wire and_1_out, and_2_out, and_3_out, and_4_out, and_5_out, and_6_out, and_7_out, and_8_out, and_9_out,
       and_10_out, and_11_out, and_12_out, and_13_out, and_14_out, full_sub_1_bit, full_sub_1_bout,
       full_sub_2_bit, full_sub_2_bout, half_sub_1_bit, half_sub_1_borrow, or_1_out, or_2_out, xor_1_out,
       xor_2_out;

  and and_1 (and_1_out, Index[0], Index[2]);
  and and_2 (and_2_out, Index[2], Index[1]);
  and and_3 (and_3_out, and_2_out, ~Index[0]);  // AND_Gate
  and and_4 (and_4_out, ~and_1_out, Index[0]);  // AND_Gate
  and and_5 (and_5_out, Index[2], ~and_1_out);  // AND_Gate
  xor xor_1 (xor_1_out, Head[2], 1'b1);
  and and_6 (and_6_out, Head[2], 1'b1);
  or or_1 (or_1_out, and_3_out, and_4_out);
  and and_7 (and_7_out, Index[1], ~and_3_out);  // AND_Gate
  and and_8 (and_8_out, and_5_out, ~and_3_out);  // AND_Gate
  half_sub half_sub_1 (.A(Head[0]), .B(or_1_out), .\bit (half_sub_1_bit), .borrow(half_sub_1_borrow));
  full_sub full_sub_1 (
    .A(Head[1]), .B(and_7_out), .Bin(half_sub_1_borrow), .\bit (full_sub_1_bit), .Bout(full_sub_1_bout));
  full_sub full_sub_2 (
    .A(xor_1_out), .B(and_8_out), .Bin(full_sub_1_bout), .\bit (full_sub_2_bit), .Bout(full_sub_2_bout));
  and and_9 (and_9_out, half_sub_1_bit, full_sub_2_bit);
  and and_10 (and_10_out, full_sub_2_bit, full_sub_1_bit);
  xor xor_2 (xor_2_out, full_sub_2_bout, and_6_out);
  and and_11 (and_11_out, and_10_out, ~half_sub_1_bit);  // AND_Gate
  and and_12 (and_12_out, ~and_9_out, half_sub_1_bit);  // AND_Gate
  and and_13 (and_13_out, ~and_9_out, full_sub_2_bit);  // AND_Gate
  or or_2 (or_2_out, and_11_out, and_12_out);
  or or_3 (out_index[0], or_2_out, xor_2_out);
  and and_14 (and_14_out, ~and_11_out, full_sub_1_bit);  // AND_Gate
  and and_15 (out_index[2], ~and_11_out, and_13_out);  // AND_Gate
  or or_4 (out_index[1], and_14_out, xor_2_out);
endmodule

module Head (
  input  up_down,
  input  T,
  input  clk,
  input  Reset,
  output [2:0] Out_head
);

  wire and_1_out, and_2_out, and_3_out, and_4_out, and_5_out, and_6_out, and_7_out, and_8_out, and_9_out,
       and_10_out, not_1_out, or_1_out, or_2_out, or_3_out, or_4_out, or_5_out, t_trigger_1_nq,
       t_trigger_2_nq;

  and and_1 (and_1_out, Out_head[0], ~Out_head[1]);  // AND_Gate
  and and_2 (and_2_out, Out_head[0], Out_head[1]);
  and and_3 (and_3_out, and_2_out, Out_head[2]);
  and and_4 (and_4_out, and_1_out, Out_head[2]);
  or or_1 (or_1_out, and_4_out, Reset);
  and and_5 (and_5_out, or_4_out, T);
  and and_6 (and_6_out, or_5_out, T);
  or or_2 (or_2_out, and_3_out, or_1_out);
  or or_3 (or_3_out, and_3_out, or_1_out);
  T_trigger t_trigger_1 (.Set(1'b0), .T(T), .clk(clk), .Reset(or_2_out), .Q(Out_head[0]), .nQ(t_trigger_1_nq));
  T_trigger t_trigger_2 (.Set(1'b0), .T(and_5_out), .clk(clk), .Reset(or_3_out), .Q(Out_head[1]), .nQ(t_trigger_2_nq));
  T_trigger t_trigger_3 (.Set(and_3_out), .T(and_6_out), .clk(clk), .Reset(or_1_out), .Q(Out_head[2]));  // open: nQ
  not not_1 (not_1_out, up_down);
  and and_7 (and_7_out, Out_head[0], up_down);
  and and_8 (and_8_out, t_trigger_1_nq, not_1_out);
  or or_4 (or_4_out, and_7_out, and_8_out);
  and and_9 (and_9_out, Out_head[1], and_7_out);
  and and_10 (and_10_out, t_trigger_2_nq, and_8_out);
  or or_5 (or_5_out, and_9_out, and_10_out);
endmodule

module ind_down (
  input  [2:0] ind,
  input  down_flag,
  output [2:0] ind_out
);

  and and_1 (ind_out[0], ind[0], down_flag);
  and and_2 (ind_out[1], ind[1], down_flag);
  and and_3 (ind_out[2], ind[2], down_flag);
endmodule

module gate (
  input  comO,
  input  comI,
  input  clk,
  output open_gate_n
);

  wire and_1_out, and_2_out, or_1_out;

  and and_1 (and_1_out, comO, comI);
  and and_2 (and_2_out, comI, ~comO);  // AND_Gate
  or or_1 (or_1_out, and_1_out, and_2_out);
  and and_3 (open_gate_n, or_1_out, clk);
endmodule
